// Logisim project half addder.circ as structural Verilog: 1 circuit, main circuit main
module main (
  input  a,
  input  b,
  output x,
  output y
);

  xor xor_1 (x, a, b);
  and and_1 (y, b, a);

  // Notes on the sheet:
  //   HALF Adder
endmodule
